# Fritzing sketch panometer (saved by Fritzing 0.9.3b)
breadboards: 1

parts:
  MCU1 = Raspberry Pi Zero
  DHT1 = DHT11 Humitidy and Temperature Sensor
  Part1 = Adafruit VL6180X Time of Flight Distance Sensor [part_number="Adafruit #3316"]

nets:
  VDD: MCU1.pin_1, MCU1.pin_17, DHT1.VDD, Part1.VIN
  N1: MCU1.pin_3, Part1.SDA
  N2: MCU1.pin_5, Part1.SCL
  GND: MCU1.pin_9, DHT1.GND, Part1.GND
  N3: MCU1.pin_15, DHT1.DATA

custom parts:
  DHT11 Humitidy and Temperature Sensor: DHT11 Humidity and Temperature Sensor
  Adafruit VL6180X Time of Flight Distance Sensor: The VL6180X is a Time of Flight distance sensor like no other you've used! The sensor contains a very tiny invisible laser source, and a matching sensor. The VL6180X can detect the "time of flight", or how long the light has taken to bounce back to the sensor. Since it uses a very narrow light source, it is good for determining distance of only the surface directly in front of it. Unlike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
