# Fritzing sketch panometer-rpi (saved by Fritzing 0.9.3b)
circuit board: 6.61249cm x 6.42669cm
breadboards: 1

parts:
  DHT1 = DHT11 Humitidy and Temperature Sensor
  Part1 = Adafruit VL6180X Time of Flight Distance Sensor [part_number="Adafruit #3316"]
  MCU1 = Raspberry Pi Zero

nets:
  VDD: DHT1.VDD, Part1.VIN, MCU1.pin_1, MCU1.pin_17
  N1: DHT1.DATA, MCU1.pin_15
  GND: DHT1.GND, Part1.GND, MCU1.pin_9
  N2: Part1.SCL, MCU1.pin_5
  N3: Part1.SDA, MCU1.pin_3

custom parts:
  DHT11 Humitidy and Temperature Sensor: DHT11 Humidity and Temperature Sensor
  Adafruit VL6180X Time of Flight Distance Sensor: The VL6180X is a Time of Flight distance sensor like no other you've used! The sensor contains a very tiny invisible laser source, and a matching sensor. The VL6180X can detect the "time of flight", or how long the light has taken to bounce back to the sensor. Since it uses a very narrow light source, it is good for determining distance of only the surface directly in front of it. Unlike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
